// Logisim project cpu.circ as structural Verilog: 19 circuits, main circuit CPU
module CPU (
  input  [15:0] From_Instr_Mem,
  input  clk,
  output [15:0] r0,
  output [15:0] r1,
  output [15:0] r2,
  output [15:0] r3,
  output [15:0] Display_0,
  output [15:0] Display_1,
  output [15:0] Data_Mem_Data,
  output [15:0] To_Instr_Mem,
  output [15:0] Data_Mem_Addr,
  output Data_Mem_Write
);

  wire arithmetic_logic_unit_1_p3, arithmetic_logic_unit_1_p5, instruction_decoder_1_regdest,
       instruction_decoder_1_regwrite, register_file_1_p1, register_file_1_p13;
  wire [1:0] instruction_decoder_1_out_4, instruction_decoder_1_out_5, instruction_decoder_1_out_6,
       multiplexer_1_out;
  wire [15:0] arithmetic_logic_unit_1_p2, arithmetic_logic_unit_1_p4, arithmetic_logic_unit_1_p6,
       data_memory_1_dataout, register_file_1_p14, WriteData;

  Instruction_Decoder instruction_decoder_1 (
    .RegDest(instruction_decoder_1_regdest), .out_4(instruction_decoder_1_out_4),
    .out_5(instruction_decoder_1_out_5), .out_6(instruction_decoder_1_out_6),
    .RegWrite(instruction_decoder_1_regwrite));  // open: in_1, Imm_Addr, SignExtend
  Multiplexer #(.width(2), .enable("false")) multiplexer_1 (
    .in0(instruction_decoder_1_out_5), .in1(instruction_decoder_1_out_6), .out(multiplexer_1_out),
    .sel(instruction_decoder_1_regdest));
  // Register_File register_file_1: pin names not known; wires that end beside it: register_file_1_p1, multiplexer_1_out, instruction_decoder_1_out_6, instruction_decoder_1_out_4, WriteData, instruction_decoder_1_regwrite, register_file_1_p1, r0, r1, clk, r2, r3, register_file_1_p13, register_file_1_p14
  // Arithmetic_Logic_Unit arithmetic_logic_unit_1: pin names not known; wires that end beside it: register_file_1_p13, arithmetic_logic_unit_1_p2, arithmetic_logic_unit_1_p3, arithmetic_logic_unit_1_p4, arithmetic_logic_unit_1_p5, arithmetic_logic_unit_1_p6
  Multiplexer #(.width(16), .enable("false")) multiplexer_2 (
    .in0(register_file_1_p14), .out(arithmetic_logic_unit_1_p2));  // open: in1, sel
  Multiplexer #(.width(16), .enable("false")) multiplexer_3 (
    .in0(data_memory_1_dataout), .in1(arithmetic_logic_unit_1_p4), .out(WriteData),
    .sel(arithmetic_logic_unit_1_p5));
  Data_Memory data_memory_1 (
    .DataIn(arithmetic_logic_unit_1_p4), .Address(arithmetic_logic_unit_1_p6),
    .DataOut(data_memory_1_dataout), .MemWrite(Data_Mem_Write));  // open: Reset

  // Other names for the same wires on the sheet: d0[15:0] = Display_0; d1[15:0] = Display_1;
  //   MemWrite = Data_Mem_Write

  // Notes on the sheet:
  //   This is the current PC that you need to send as OUTPUT
  //   This is the instruction that you would receive as INPUT
  //   rt
  //   This is a CLK that is an INPUT driven from the harness.
  //   Remember, this circuit is loaded from the harness to be tested!
  //   DO NOT CHANGE THE LOCATIONS OF THE INPUTS OR OUTPUTS! IF YOU DO SO, YOU NEED TO MAKE SURE THE PINS ARE IN THE RIGHT PLACES!
  //   RegDest
  //   rd
  //   rs
  //   RegWrite
  //   These are OUTPUTS of the circuit
  //   These are OUTPUTS of the circuit
endmodule

module Data_Memory (
  input  [15:0] DataIn,
  input  [15:0] Address,
  input  Reset,
  input  MemWrite,
  output [15:0] DataOut
);

  wire clk_out, not_1_out;

  Clock clk (.out(clk_out));
  assign DataOut = MemWrite ? DataIn : 16'bz;  // Controlled_Buffer controlled_buffer_1
  RAM #(.addrWidth(16), .dataWidth(16)) ram_1 (
    .addr(Address), .data(DataOut), .sel(1'b1), .clk(clk_out), .ld(not_1_out), .clr(Reset));
  not not_1 (not_1_out, MemWrite);
endmodule

module Instruction_Decoder (
  input  [15:0] in_1,
  output SignExtend,
  output RegDest,
  output [1:0] out_4,
  output [1:0] out_5,
  output [1:0] out_6,
  output RegWrite,
  output Imm_Addr
);

  wire I_Imm_Addr, I_RegDest, I_RegWrite, I_SignExt, J_Imm_Addr, J_RegDest, J_RegWrite, J_SignExt,
       R_Imm_Addr, R_RegDest, R_RegWrite, R_SignExt;
  wire [1:0] I_rd, I_rs, I_rt, J_rd, J_rs, J_rt, opcode, R_rd, R_rs, R_rt;

  R_type_Instruction_Decode r_type_instruction_decode_1 (
    .in_1(in_1), .rd(R_rd), .rt(R_rt), .rs(R_rs), .RegWrite(R_RegWrite), .RegDest(R_RegDest),
    .Imm_Addr(R_Imm_Addr), .Signed(R_SignExt));
  J_type_Instruction_Decoder j_type_instruction_decoder_1 (
    .in_1(in_1), .rd(J_rd), .rt(J_rt), .rs(J_rs), .RegWrite(J_RegWrite), .RegDest(J_RegDest),
    .Imm_Addr(J_Imm_Addr), .Signed(J_SignExt));
  Type_Decoder type_decoder_1 (.in_1(in_1), .Type(opcode));
  I_type_Instruction_Decoder i_type_instruction_decoder_1 (
    .in_1(in_1), .rd(I_rd), .rt(I_rt), .rs(I_rs), .SignOrUnsign(I_SignExt), .RegWrite(I_RegWrite),
    .RegDest(I_RegDest), .Imm_Addr(I_Imm_Addr));
  Multiplexer #(.select(2), .width(2), .enable("false")) multiplexer_1 (
    .in0(R_rs), .in1(J_rs), .in2(I_rs), .out(out_4), .sel(opcode));  // open: in3
  Multiplexer #(.select(2), .width(2), .enable("false")) multiplexer_2 (
    .in0(R_rd), .in1(J_rd), .in2(I_rd), .out(out_5), .sel(opcode));  // open: in3
  Multiplexer #(.select(2), .width(2), .enable("false")) multiplexer_3 (
    .in0(R_rt), .in1(J_rt), .in2(I_rt), .out(out_6), .sel(opcode));  // open: in3
  Multiplexer #(.select(2), .enable("false")) multiplexer_4 (
    .in0(R_RegDest), .in1(J_RegDest), .in2(I_RegDest), .out(RegDest), .sel(opcode));  // open: in3
  Multiplexer #(.select(2), .enable("false")) multiplexer_5 (
    .in1(R_RegWrite), .in2(J_RegWrite), .in3(I_RegWrite), .out(RegWrite), .sel(opcode));  // open: in0
  Multiplexer #(.select(2), .enable("false")) multiplexer_6 (
    .in0(I_Imm_Addr), .in1(I_Imm_Addr), .in2(I_Imm_Addr), .out(Imm_Addr), .sel(opcode));  // open: in3
  Multiplexer #(.select(2), .enable("false")) multiplexer_7 (
    .in0(R_SignExt), .in1(J_SignExt), .in2(I_SignExt), .out(SignExtend), .sel(opcode));  // open: in3

  // Other names for the same wires on the sheet: Instruction_In[15:0] = in_1; rd[1:0] = out_5; rs[1:0] = out_4;
  //   rt[1:0] = out_6

  // Notes on the sheet:
  //   0: write to rd
  //   1: write to rt
endmodule

// R-type decoder
module R_type_Instruction_Decode (
  input  [15:0] in_1,
  output [1:0] rd,
  output [1:0] rt,
  output [1:0] rs,
  output RegWrite,
  output RegDest,
  output Imm_Addr,
  output Signed
);

  BitSelector #(.width(16), .group(2)) bitselector_1 (.in(in_1), .out(rd), .sel(3'b011));
  BitSelector #(.width(16), .group(2)) bitselector_2 (.in(in_1), .out(rt), .sel(3'b100));
  BitSelector #(.width(16), .group(2)) bitselector_3 (.in(in_1), .out(rs), .sel(3'b101));

  assign Imm_Addr = 1'b0;
  assign RegDest = 1'b0;
  assign RegWrite = 1'b1;
  assign Signed = 1'b0;

  // Notes on the sheet:
  //   (enable write to register)
  //   (select rd as destination register)
endmodule

// I-type decoder
module I_type_Instruction_Decoder (
  input  [15:0] in_1,
  output [1:0] rd,
  output [1:0] rt,
  output [1:0] rs,
  output SignOrUnsign,
  output RegWrite,
  output RegDest,
  output Imm_Addr
);

  wire addiRW, addiSOU, andiRW, andiSOU, beqRW, beqSOU, bneRW, bneSOU, dispRW, dispSOU, luiRW, luiSOU, lwRW,
       lwSOU, oriRW, oriSOU, swRW, swSOU;
  wire [3:0] InstrSelect;

  beq beq_1 (.Sign(beqSOU), .RegWrite(beqRW));
  ori ori_1 (.Sign(oriSOU), .RegWrite(oriRW));
  lui lui_1 (.Sign(luiSOU), .RegWrite(luiRW));
  BitSelector #(.width(16), .group(4)) bitselector_1 (.in(in_1), .out(InstrSelect), .sel(2'b11));
  BitSelector #(.width(16), .group(2)) bitselector_2 (.in(in_1), .out(rt), .sel(3'b100));
  addi addi_1 (.Sign(addiSOU), .RegWrite(addiRW));
  bne bne_1 (.Sign(bneSOU), .RegWrite(bneRW));
  lw lw_1 (.Sign(lwSOU), .RegWrite(lwRW));
  BitSelector #(.width(16), .group(2)) bitselector_3 (.in(in_1), .out(rs), .sel(3'b101));
  andi andi_1 (.Sign(andiSOU), .RegWrite(andiRW));
  sw sw_1 (.Sign(swSOU), .RegWrite(swRW));
  disp disp_1 (.Sign(dispSOU), .RegWrite(dispRW));
  Multiplexer #(.select(4), .enable("false")) multiplexer_1 (
    .in4(beqSOU), .in5(addiSOU), .in6(andiSOU), .in7(oriSOU), .in8(bneSOU), .in9(swSOU), .in10(luiSOU),
    .in11(lwSOU), .in12(dispSOU), .out(SignOrUnsign), .sel(InstrSelect));  // open: in0, in1, in2, in3, in13, in14, in15
  Multiplexer #(.select(4), .enable("false")) multiplexer_2 (
    .in4(beqRW), .in5(addiRW), .in6(andiRW), .in7(oriRW), .in8(bneRW), .in9(swRW), .in10(luiRW), .in11(lwRW),
    .in12(dispRW), .out(RegWrite), .sel(InstrSelect));  // open: in0, in1, in2, in3, in13, in14, in15

  assign Imm_Addr = 1'b0;
  assign rd = 2'b11;
  assign RegDest = 1'b1;

  // Notes on the sheet:
  //   (rd is not used)
  //   (select rt as destination register)
endmodule

// J-type decoder
module J_type_Instruction_Decoder (
  input  [15:0] in_1,
  output [1:0] rd,
  output [1:0] rt,
  output [1:0] rs,
  output RegWrite,
  output RegDest,
  output Imm_Addr,
  output Signed
);

  wire [1:0] bitselector_1_out;

  BitSelector #(.width(16), .group(2)) bitselector_1 (.in(in_1), .out(bitselector_1_out), .sel(3'b110));

  assign Imm_Addr = 1'b0;
  assign rd = 2'b00;
  assign RegDest = 1'b0;
  assign RegWrite = 1'b0;
  assign rt = 2'b00;
  assign Signed = 1'b0;
endmodule

module beq (
  output Sign,
  output RegWrite
);


  assign RegWrite = 1'b0;
  assign Sign = 1'b1;
endmodule

module addi (
  output Sign,
  output RegWrite
);


  assign RegWrite = 1'b1;
  assign Sign = 1'b1;
endmodule

module andi (
  output Sign,
  output RegWrite
);


  assign RegWrite = 1'b1;
  assign Sign = 1'b0;
endmodule

module ori (
  output Sign,
  output RegWrite
);


  assign RegWrite = 1'b1;
  assign Sign = 1'b0;
endmodule

module bne (
  output Sign,
  output RegWrite
);


  assign RegWrite = 1'b0;
  assign Sign = 1'b1;
endmodule

module sw (
  output Sign,
  output RegWrite
);


  assign RegWrite = 1'b0;
  assign Sign = 1'b1;
endmodule

module lui (
  output Sign,
  output RegWrite
);


  assign RegWrite = 1'b1;
  assign Sign = 1'b0;
endmodule

module lw (
  output Sign,
  output RegWrite
);


  assign RegWrite = 1'b1;
  assign Sign = 1'b1;
endmodule

module disp (
  output Sign,
  output RegWrite
);


  assign RegWrite = 1'b0;
  assign Sign = 1'b0;
endmodule

module jal (
  input  [15:0] in_1,
  output [11:0] target_addr
);

  BitSelector #(.width(16), .group(12)) bitselector_1 (.in(in_1), .out(target_addr), .sel(1'b0));
endmodule

module j (
  input  [15:0] in_1,
  output [11:0] target_addr
);

  BitSelector #(.width(16), .group(12)) bitselector_1 (.in(in_1), .out(target_addr), .sel(1'b0));
endmodule

module jr (
  input  [15:0] in_1,
  output [1:0] rs
);

  BitSelector #(.width(16), .group(2)) bitselector_1 (.in(in_1), .out(rs), .sel(3'b101));
endmodule

module Type_Decoder (
  input  [15:0] in_1,
  output [1:0] Type
);

  wire [3:0] opcode;

  BitSelector #(.width(16), .group(4)) bitselector_1 (.in(in_1), .out(opcode), .sel(2'b11));
  Multiplexer #(.select(4), .width(2), .enable("false")) multiplexer_1 (
    .in0(2'b00), .in1(2'b01), .in2(2'b01), .in3(2'b01), .in4(2'b10), .in5(2'b10), .in6(2'b10), .in7(2'b10),
    .in8(2'b10), .in9(2'b10), .in10(2'b10), .in11(2'b10), .in12(2'b10), .out(Type), .sel(opcode));  // open: in13, in14, in15
endmodule
